// Logisim project FINAL_CA_LAB03_TASK.circ as structural Verilog: 1 circuit, main circuit main
module main (
  input  [23:0] in_1,
  input  RESET
);

  wire clock_1_out;
  wire [1:0] counter_1_q;
  wire [2:0] rom_1_data_2;
  wire [3:0] rom_1_data;
  wire [23:0] multiplexer_1_out, register_1_q, register_2_q, register_3_q, register_4_q, undriven;

  Counter #(.width(2), .max('h3)) counter_1 (
    .Q(counter_1_q), .clk(clock_1_out), .clr(RESET));  // open: load, D, count, carry
  Clock clock_1 (.out(clock_1_out));
  Multiplexer #(.select(3), .width(24), .enable("false")) multiplexer_1 (
    .in0(undriven), .in1(register_1_q), .in2(register_2_q), .in3(register_3_q), .in4(register_4_q),
    .out(multiplexer_1_out), .sel(rom_1_data_2));  // open: in5, in6, in7
  ROM #(.addrWidth(2), .dataWidth(7)) rom_1 (.addr(counter_1_q), .data({rom_1_data_2, rom_1_data}), .sel(1'b1));
  Register #(.width(24)) register_1 (
    .D(multiplexer_1_out), .en(rom_1_data[3]), .Q(register_1_q), .clk(clock_1_out), .clr(RESET));
  Register #(.width(24)) register_2 (
    .D(multiplexer_1_out), .en(rom_1_data[2]), .Q(register_2_q), .clk(clock_1_out), .clr(RESET));
  Register #(.width(24)) register_3 (
    .D(multiplexer_1_out), .Q(register_3_q), .clk(clock_1_out), .clr(RESET));  // open: en
  Register #(.width(24)) register_4 (
    .D(multiplexer_1_out), .en(rom_1_data[0]), .Q(register_4_q), .clk(clock_1_out), .clr(RESET));

  // Notes on the sheet:
  //   24_BIT_INPUT
  //   CLK
  //   ROM
  //   contents of rom_1 (hex, n*v repeats v):
  //   8 14 21 42
  //   A
  //   B
  //   C
  //   D
endmodule
