// Logisim project FINAL_CA_SEQUENCE_TASK.circ as structural Verilog: 1 circuit, main circuit main
module main (
  input  [23:0] in_1,
  input  RESET
);

  wire clock_1_out, undriven;
  wire [1:0] counter_1_q;
  wire [6:0] rom_1_data;
  wire [23:0] A_q, B_q, C_q, D_q, multiplexer_1_out;

  Counter #(.width(2), .max('h3)) counter_1 (
    .Q(counter_1_q), .clk(clock_1_out), .clr(undriven));  // open: load, D, count, carry
  Multiplexer #(.select(3), .width(24)) multiplexer_1 (
    .in0(in_1), .in1(A_q), .in2(B_q), .in3(C_q), .in4(D_q), .out(multiplexer_1_out), .sel(rom_1_data[6:4]));  // open: in5, in6, in7, en
  Clock clock_1 (.out(clock_1_out));
  Register #(.width(24)) A (.D(multiplexer_1_out), .en(rom_1_data[0]), .Q(A_q), .clk(clock_1_out), .clr(undriven));
  Register #(.width(24)) B (.D(multiplexer_1_out), .en(rom_1_data[1]), .Q(B_q), .clk(clock_1_out), .clr(undriven));
  ROM #(.addrWidth(2), .dataWidth(7)) rom_1 (.addr(counter_1_q), .data(rom_1_data), .sel(1'b1));
  Register #(.width(24)) C (.D(multiplexer_1_out), .en(rom_1_data[2]), .Q(C_q), .clk(clock_1_out), .clr(undriven));
  Register #(.width(24)) D (.D(multiplexer_1_out), .en(rom_1_data[3]), .Q(D_q), .clk(clock_1_out), .clr(undriven));

  // Notes on the sheet:
  //   24_BIT_INPUT
  //   D_FF
  //   A->B->D->C
  //   CLK
  //   ROM
  //   contents of rom_1 (hex, n*v repeats v):
  //   1 12 28 44
endmodule
