// Logisim project LAB_3_ARCHITECTURE_CIR.circ as structural Verilog: 2 circuits, main circuit main
module main (
  input  [23:0] _24_BIT_input,
  input  reset
);

  wire clk_out, control_unit_1_input_a, control_unit_1_out_a_in_b, control_unit_1_out_b_in_d,
       control_unit_1_out_d_in_c;

  Clock clk (.out(clk_out));
  control_unit control_unit_1 (
    .clk(clk_out), .reset(reset), .INPUT_A(control_unit_1_input_a), .out_a_in_b(control_unit_1_out_a_in_b),
    .out_b_in_d(control_unit_1_out_b_in_d), .out_d_in_c(control_unit_1_out_d_in_c));  // open: q0, q1
  Register #(.width(24)) A (.D(_24_BIT_input), .en(control_unit_1_input_a), .clk(clk_out), .clr(reset));  // open: Q
  Register #(.width(24)) B (.D(_24_BIT_input), .en(control_unit_1_out_a_in_b), .clk(clk_out), .clr(reset));  // open: Q
  Register #(.width(24)) C (.D(_24_BIT_input), .en(control_unit_1_out_d_in_c), .clk(clk_out), .clr(reset));  // open: Q
  Register #(.width(24)) D (.D(_24_BIT_input), .en(control_unit_1_out_b_in_d), .clk(clk_out), .clr(reset));  // open: Q

  // Notes on the sheet:
  //   CU
endmodule

module control_unit (
  input  clk,
  input  reset,
  output INPUT_A,
  output out_a_in_b,
  output out_b_in_d,
  output out_d_in_c,
  output q0,
  output q1
);

  wire [5:4] rom_1_data;

  D_Flip_Flop D0 (.clk(clk), .D(rom_1_data[4]), .Q(q0), .en(1'b1), .reset(reset));  // open: Qn, preset
  D_Flip_Flop D1 (.clk(clk), .D(rom_1_data[5]), .Q(q1), .en(1'b1), .reset(reset));  // open: Qn, preset
  ROM #(.addrWidth(2), .dataWidth(6)) rom_1 (
    .addr({q1, q0}), .data({rom_1_data, INPUT_A, out_a_in_b, out_b_in_d, out_d_in_c}));  // open: sel

  // Notes on the sheet:
  //   contents of rom_1 (hex, n*v repeats v):
  //   18 24 32 1
endmodule
